// Logisim project 2 Bit Parallel Adder.circ as structural Verilog: 1 circuit, main circuit main
module main (
  input  A0,
  input  B0,
  input  A1,
  input  B1,
  output Sum0,
  output Sum1,
  output Carry0
);

  wire and_1_out, and_2_out, and_3_out, and_4_out, or_1_out, xor_2_out;

  xor xor_1 (Sum0, A0, B0);
  and and_1 (and_1_out, A0, B0);
  xor xor_2 (xor_2_out, A1, B1);
  and and_2 (and_2_out, A1, B1);
  and and_3 (and_3_out, A0, B0);
  or or_1 (or_1_out, A1, B1);
  xor xor_3 (Sum1, and_1_out, xor_2_out);
  and and_4 (and_4_out, and_3_out, or_1_out);
  or or_2 (Carry0, and_2_out, and_4_out);
endmodule
