// Logisim project 3 Bit Ripple Carry Adder.circ as structural Verilog: 1 circuit, main circuit main
module main (
  input  A0,
  input  B0,
  input  A1,
  input  B1,
  input  A2,
  input  B2,
  output Sum0,
  output Sum1,
  output Sum2,
  output Carry0
);

  wire and_1_out, and_2_out, and_3_out, and_4_out, and_5_out, and_6_out, and_7_out, or_1_out, xor_1_out,
       xor_2_out;

  xor xor_1 (xor_1_out, A1, B1);
  and and_1 (and_1_out, A1, and_7_out);
  and and_2 (and_2_out, A1, B1);
  and and_3 (and_3_out, B1, and_7_out);
  xor xor_2 (xor_2_out, A2, B2);
  and and_4 (and_4_out, A2, or_1_out);
  and and_5 (and_5_out, A2, B2);
  and and_6 (and_6_out, B2, or_1_out);
  xor xor_3 (Sum0, A0, B0);
  and and_7 (and_7_out, A0, B0);
  xor xor_4 (Sum1, xor_1_out, and_7_out);
  or or_1 (or_1_out, and_1_out, and_2_out, and_3_out);
  xor xor_5 (Sum2, xor_2_out, or_1_out);
  or or_2 (Carry0, and_4_out, and_5_out, and_6_out);
endmodule
