// Logisim project One_Bit_Full_Adder.circ as structural Verilog: 1 circuit, main circuit main
module main (
  input  A0,
  input  B0,
  output Sum0,
  output Carry0
);

  xor xor_1 (Sum0, A0, B0);
  and and_1 (Carry0, A0, B0);
endmodule
