// Logisim project Small Memory Chip.circ as structural Verilog: 1 circuit, main circuit main
module main (
  input  [1:0] Data_In,
  input  [1:0] Address,
  input  Write,
  output [1:0] Data_Out
);

  wire and_1_out, and_2_out, and_3_out, and_4_out, and_5_out, and_6_out, and_7_out, and_8_out, and_9_out,
       and_10_out, and_11_out, and_12_out, and_13_out, and_14_out, and_15_out, and_16_out, d_ff_1_q,
       d_ff_2_q, d_ff_3_q, d_ff_4_q, d_ff_5_q, d_ff_6_q, d_ff_7_q, d_ff_8_q, or_1_out, or_2_out, or_4_out,
       or_5_out;

  and and_1 (and_1_out, ~Address[0], ~Address[1]);  // AND_Gate
  and and_2 (and_2_out, Address[0], ~Address[1]);  // AND_Gate
  and and_3 (and_3_out, ~Address[0], Address[1]);  // AND_Gate
  and and_4 (and_4_out, Address[0], Address[1]);
  and and_5 (and_5_out, and_1_out, Write);
  and and_6 (and_6_out, and_2_out, Write);
  and and_7 (and_7_out, and_3_out, Write);
  and and_8 (and_8_out, and_4_out, Write);
  D_Flip_Flop d_ff_1 (.clk(and_5_out), .D(Data_In[1]), .Q(d_ff_1_q));  // open: Qn, preset, en, reset
  and and_9 (and_9_out, d_ff_1_q, and_1_out);
  D_Flip_Flop d_ff_2 (.clk(and_6_out), .D(Data_In[1]), .Q(d_ff_2_q));  // open: Qn, preset, en, reset
  and and_10 (and_10_out, d_ff_2_q, and_2_out);
  or or_1 (or_1_out, and_10_out, and_9_out);
  D_Flip_Flop d_ff_3 (.clk(and_7_out), .D(Data_In[1]), .Q(d_ff_3_q));  // open: Qn, preset, en, reset
  and and_11 (and_11_out, d_ff_3_q, and_3_out);
  or or_2 (or_2_out, and_11_out, or_1_out);
  D_Flip_Flop d_ff_4 (.clk(and_8_out), .D(Data_In[1]), .Q(d_ff_4_q));  // open: Qn, preset, en, reset
  and and_12 (and_12_out, d_ff_4_q, and_4_out);
  or or_3 (Data_Out[1], and_12_out, or_2_out);
  D_Flip_Flop d_ff_5 (.clk(and_5_out), .D(Data_In[0]), .Q(d_ff_5_q));  // open: Qn, preset, en, reset
  D_Flip_Flop d_ff_6 (.clk(and_6_out), .D(Data_In[0]), .Q(d_ff_6_q));  // open: Qn, preset, en, reset
  D_Flip_Flop d_ff_7 (.clk(and_7_out), .D(Data_In[0]), .Q(d_ff_7_q));  // open: Qn, preset, en, reset
  D_Flip_Flop d_ff_8 (.clk(and_8_out), .D(Data_In[0]), .Q(d_ff_8_q));  // open: Qn, preset, en, reset
  and and_13 (and_13_out, d_ff_5_q, and_1_out);
  and and_14 (and_14_out, d_ff_6_q, and_2_out);
  or or_4 (or_4_out, and_14_out, and_13_out);
  and and_15 (and_15_out, d_ff_7_q, and_3_out);
  or or_5 (or_5_out, and_15_out, or_4_out);
  and and_16 (and_16_out, d_ff_8_q, and_4_out);
  or or_6 (Data_Out[0], and_16_out, or_5_out);
endmodule
