// Logisim project Homework4.circ as structural Verilog: 1 circuit, main circuit main
module main (
  input  [7:0] Data,
  input  Data_2_A,
  input  Bus_2_A,
  input  A_in,
  input  A_out,
  input  B_in,
  input  B_out,
  input  C_in,
  input  C_out,
  output [7:0] Bus
);

  wire [7:0] A_q, and_1_out, and_2_out, B_q, C_q, or_1_out;

  assign and_1_out = Data & {8{Data_2_A}};  // AND_Gate and_1, 8 bits wide
  assign and_2_out = {8{Bus_2_A}} & Bus;  // AND_Gate and_2, 8 bits wide
  assign or_1_out = and_1_out | and_2_out;  // OR_Gate or_1, 8 bits wide
  Register A (.D(or_1_out), .Q(A_q), .clk(A_in));  // open: en, clr
  assign Bus = A_out ? A_q : 8'bz;  // Controlled_Buffer controlled_buffer_1
  Register B (.D(Bus), .Q(B_q), .clk(B_in));  // open: en, clr
  assign Bus = B_out ? B_q : 8'bz;  // Controlled_Buffer controlled_buffer_2
  assign Bus = C_out ? C_q : 8'bz;  // Controlled_Buffer controlled_buffer_3
  Register C (.D(Bus), .Q(C_q), .clk(C_in));  // open: en, clr
endmodule
