// Logisim project Reg_ex.circ as structural Verilog: 1 circuit, main circuit main
module main (
  input  [7:0] Data,
  input  Reg_in,
  input  Reg_out,
  output [7:0] Bus
);

  wire [7:0] register_1_q;

  Register register_1 (.D(Data), .Q(register_1_q), .clk(Reg_in));  // open: en, clr
  assign Bus = Reg_out ? register_1_q : 8'bz;  // Controlled_Buffer controlled_buffer_1

  // Notes on the sheet:
  //   Reg
endmodule
