// Logisim project ALU.circ as structural Verilog: 1 circuit, main circuit main
module main (
  input  [1:0] F,
  input  [7:0] A,
  input  [7:0] B,
  input  Zero_Out,
  output [7:0] Output
);

  wire decoder_1_out2, decoder_1_out3, or_2_out;
  wire [0:0] and_7_out, or_1_out;
  wire [7:0] and_1_out, and_2_out, and_3_out, and_4_out, and_5_out, and_6_out, controlled_buffer_1_out,
       controlled_buffer_2_out, nor_1_out, not_1_out, not_2_out, xor_1_out;
  wire [7:7] decoder_1_out0, decoder_1_out1;

  Decoder #(.select(2), .enable("false")) decoder_1 (
    .out0(decoder_1_out0[7]), .out1(decoder_1_out1[7]), .out2(decoder_1_out2), .out3(decoder_1_out3), .sel(F));
  assign not_1_out = ~A;  // NOT_Gate not_1, 8 bits wide
  assign not_2_out = ~B;  // NOT_Gate not_2, 8 bits wide
  xor xor_1 (xor_1_out[0], B[0], decoder_1_out1[7]);
  xor xor_2 (xor_1_out[1], B[1], decoder_1_out1[7]);
  xor xor_3 (xor_1_out[2], B[2], decoder_1_out1[7]);
  xor xor_4 (xor_1_out[3], B[3], decoder_1_out1[7]);
  xor xor_5 (xor_1_out[4], B[4], decoder_1_out1[7]);
  xor xor_6 (xor_1_out[5], B[5], decoder_1_out1[7]);
  xor xor_7 (xor_1_out[6], B[6], decoder_1_out1[7]);
  xor xor_8 (xor_1_out[7], B[7], decoder_1_out1[7]);
  assign and_1_out = not_1_out & B;  // AND_Gate and_1, 8 bits wide
  assign and_2_out = A & not_2_out;  // AND_Gate and_2, 8 bits wide
  assign nor_1_out = ~(and_1_out | and_2_out);  // NOR_Gate nor_1, 8 bits wide
  assign controlled_buffer_1_out = decoder_1_out0[7] ? and_3_out : 8'bz;  // Controlled_Buffer controlled_buffer_1
  assign and_3_out = {8{decoder_1_out0[7]}} & A;  // AND_Gate and_3, 8 bits wide
  assign controlled_buffer_2_out = decoder_1_out0[7] ? and_4_out : 8'bz;  // Controlled_Buffer controlled_buffer_2
  assign and_4_out = {8{decoder_1_out0[7]}} & B;  // AND_Gate and_4, 8 bits wide
  assign controlled_buffer_1_out = decoder_1_out1[7] ? and_5_out : 8'bz;  // Controlled_Buffer controlled_buffer_3
  assign and_5_out = {8{decoder_1_out1[7]}} & A;  // AND_Gate and_5, 8 bits wide
  assign controlled_buffer_2_out = decoder_1_out1[7] ? and_6_out : 8'bz;  // Controlled_Buffer controlled_buffer_4
  assign and_6_out = {8{decoder_1_out1[7]}} & xor_1_out;  // AND_Gate and_6, 8 bits wide
  and and_7 (and_7_out[0], nor_1_out[0], nor_1_out[1], nor_1_out[2], nor_1_out[3], nor_1_out[4], nor_1_out[5], nor_1_out[6], nor_1_out[7]);
  or or_1 (or_1_out[0], and_7_out[0], or_2_out);
  or or_2 (or_2_out, and_2_out[0], and_2_out[1], and_2_out[2], and_2_out[3], and_2_out[4], and_2_out[5], and_2_out[6], and_2_out[7]);
  Adder adder_1 (
    .a(controlled_buffer_1_out), .b(controlled_buffer_2_out), .out(Output), .cin(decoder_1_out1[7]));  // open: cout
  assign Output = decoder_1_out2 ? {{7{Zero_Out}}, and_7_out[0]} : 8'bz;  // Controlled_Buffer controlled_buffer_5
  assign Output = decoder_1_out3 ? {{7{Zero_Out}}, or_1_out[0]} : 8'bz;  // Controlled_Buffer controlled_buffer_6
endmodule
