// Logisim project Small ALU.circ as structural Verilog: 1 circuit, main circuit main
module main (
  input  [1:0] F,
  input  [7:0] A,
  input  [7:0] B,
  output [7:0] Output
);

  wire decoder_1_out3;
  wire [7:0] adder_1_out, and_1_out, and_2_out, and_3_out, and_4_out, and_5_out, and_6_out, and_7_out,
       nor_1_out, not_1_out, not_2_out, or_1_out, subtractor_1_out;
  wire [7:7] and_8_out, and_9_out, decoder_1_out0, decoder_1_out1, decoder_1_out2;

  Decoder #(.select(2), .enable("false")) decoder_1 (
    .out0(decoder_1_out0[7]), .out1(decoder_1_out1[7]), .out2(decoder_1_out2[7]), .out3(decoder_1_out3),
    .sel(F));
  assign not_1_out = ~A;  // NOT_Gate not_1, 8 bits wide
  assign not_2_out = ~B;  // NOT_Gate not_2, 8 bits wide
  assign and_1_out = A & {8{decoder_1_out0[7]}};  // AND_Gate and_1, 8 bits wide
  Adder adder_1 (.a(and_1_out), .b(and_2_out), .out(adder_1_out));  // open: cin, cout
  assign and_2_out = B & {8{decoder_1_out0[7]}};  // AND_Gate and_2, 8 bits wide
  assign and_3_out = A & {8{decoder_1_out1[7]}};  // AND_Gate and_3, 8 bits wide
  Subtractor subtractor_1 (.a(and_3_out), .b(and_4_out), .out(subtractor_1_out));  // open: bin, bout
  assign and_4_out = B & {8{decoder_1_out1[7]}};  // AND_Gate and_4, 8 bits wide
  assign and_5_out = not_1_out & B;  // AND_Gate and_5, 8 bits wide
  assign nor_1_out = ~(and_5_out | and_6_out);  // NOR_Gate nor_1, 8 bits wide
  assign and_6_out = A & not_2_out;  // AND_Gate and_6, 8 bits wide
  assign and_7_out = {8{decoder_1_out2[7]}} & nor_1_out;  // AND_Gate and_7, 8 bits wide
  assign or_1_out = nor_1_out | and_6_out;  // OR_Gate or_1, 8 bits wide
  and and_8 (and_8_out[7], and_7_out[0], and_7_out[1], and_7_out[2], and_7_out[3], and_7_out[4], and_7_out[5], and_7_out[6], and_7_out[7]);
  and and_9 (and_9_out[7], or_1_out[0], or_1_out[1], or_1_out[2], or_1_out[3], or_1_out[4], or_1_out[5], or_1_out[6], or_1_out[7]);
  assign Output = decoder_1_out0[7] ? adder_1_out : 8'bz;  // Controlled_Buffer controlled_buffer_1
  assign Output = decoder_1_out1[7] ? subtractor_1_out : 8'bz;  // Controlled_Buffer controlled_buffer_2
  assign Output = decoder_1_out2[7] ? {8{and_8_out[7]}} : 8'bz;  // Controlled_Buffer controlled_buffer_3
  assign Output = decoder_1_out3 ? {8{and_9_out[7]}} : 8'bz;  // Controlled_Buffer controlled_buffer_4
endmodule
