// Logisim project Right Rotator.circ as structural Verilog: 1 circuit, main circuit main
module main (
  input  [3:0] A,
  input  [1:0] shamt,
  output [3:0] Y
);

  Multiplexer #(.select(2), .enable("false")) multiplexer_1 (
    .in0(A[3]), .in1(A[0]), .in2(A[1]), .in3(A[2]), .out(Y[3]), .sel(shamt));
  Multiplexer #(.select(2), .enable("false")) multiplexer_2 (
    .in0(A[2]), .in1(A[3]), .in2(A[0]), .in3(A[1]), .out(Y[2]), .sel(shamt));
  Multiplexer #(.select(2), .enable("false")) multiplexer_3 (
    .in0(A[1]), .in1(A[2]), .in2(A[3]), .in3(A[0]), .out(Y[1]), .sel(shamt));
  Multiplexer #(.select(2), .enable("false")) multiplexer_4 (
    .in0(A[0]), .in1(A[1]), .in2(A[2]), .in3(A[3]), .out(Y[0]), .sel(shamt));
endmodule
