// Logisim project Incrementer.circ as structural Verilog: 1 circuit, main circuit main
module main (
  input  in_1,
  input  [7:0] A,
  output [7:0] Y
);

  wire adder_1_cout, adder_2_cout, adder_3_cout, adder_4_cout, adder_5_cout;

  Adder #(.width(1)) adder_1 (.a(A[2]), .b(in_1), .out(Y[2]), .cout(adder_1_cout));  // open: cin
  Adder #(.width(1)) adder_2 (.a(adder_1_cout), .b(A[3]), .out(Y[3]), .cout(adder_2_cout));  // open: cin
  Adder #(.width(1)) adder_3 (.a(adder_2_cout), .b(A[4]), .out(Y[4]), .cout(adder_3_cout));  // open: cin
  Adder #(.width(1)) adder_4 (.a(adder_3_cout), .b(A[5]), .out(Y[5]), .cout(adder_4_cout));  // open: cin
  Adder #(.width(1)) adder_5 (.a(adder_4_cout), .b(A[6]), .out(Y[6]), .cout(adder_5_cout));  // open: cin
  Adder #(.width(1)) adder_6 (.a(adder_5_cout), .b(A[7]), .out(Y[7]));  // open: cin, cout

  assign Y[1:0] = A[1:0];
endmodule
